// Logisim project input_validator.circ as structural Verilog: 1 circuit, main circuit main
module main (
  input  [8:0] exp1,
  input  [31:0] frac1,
  input  [8:0] exp2,
  input  [31:0] frac2,
  output NaN_input1,
  output Denormalized_input1,
  output [31:0] Valid_Fraction1,
  output Nan_input2,
  output denormalized_input2,
  output [31:0] valid_fraction2
);

  wire input1_check_exponent_all_1, input1_check_exponent_contains_1, input1_check_fraction_contains_1,
       Input2_check_exponent_all_1, Input2_check_exponent_contains_1, Input2_check_fraction_contains_1,
       or_1_out, or_2_out;
  wire [31:0] input1_fraction_2, Input2_fraction_2;

  single_input_check_main input1 (
    .exponent(exp1), .fraction(frac1), .check_exponent_all_1(input1_check_exponent_all_1),
    .check_exponent_contains_1(input1_check_exponent_contains_1), .fraction_2(input1_fraction_2),
    .check_fraction_contains_1(input1_check_fraction_contains_1));
  single_input_check_main Input2 (
    .exponent(exp2), .fraction(frac2), .check_exponent_all_1(Input2_check_exponent_all_1),
    .check_exponent_contains_1(Input2_check_exponent_contains_1), .fraction_2(Input2_fraction_2),
    .check_fraction_contains_1(Input2_check_fraction_contains_1));
  // check_single_input_flags_main main_1: pin names not known; wires that end beside it: input1_check_exponent_all_1, input1_check_fraction_contains_1, input1_check_exponent_contains_1, NaN_input1, Denormalized_input1
  // check_single_input_flags_main main_2: pin names not known; wires that end beside it: Input2_check_exponent_all_1, Input2_check_fraction_contains_1, Input2_check_exponent_contains_1, Nan_input2, denormalized_input2
  or or_1 (or_1_out, Denormalized_input1, NaN_input1);
  or or_2 (or_2_out, Nan_input2, denormalized_input2);
  Multiplexer #(.width(32)) multiplexer_1 (
    .in0(input1_fraction_2), .in1({32{1'b0}}), .out(Valid_Fraction1), .sel(or_1_out));  // open: en
  Multiplexer #(.width(32)) multiplexer_2 (
    .in0(Input2_fraction_2), .in1({32{1'b0}}), .out(valid_fraction2), .sel(or_2_out));  // open: en
endmodule
