// Logisim project return_fraction.circ as structural Verilog: 1 circuit, main circuit main
module main (
  input  sf2,
  input  sf1,
  input  Selection_bit,
  input  lf1,
  input  lf2,
  output out_6,
  output out_7
);

  // _74157 74157_1: pin names not known; wires that end beside it: Selection_bit, lf1, lf2, out_7, 1'b0, 1'b1, 1'b0, sf1, sf2, out_6
endmodule
