// Logisim project single_input_check.circ as structural Verilog: 2 circuits, main circuit main
module main (
  input  [8:0] exponent,
  input  [31:0] fraction,
  output check_exponent_all_1,
  output check_exponent_contains_1,
  output [31:0] fraction_2,
  output check_fraction_contains_1
);

  wire [31:0] shifter_1_out;

  Shifter #(.width(32)) shifter_1 (.in(fraction), .\dist (5'b00010), .out(shifter_1_out));
  _1_checker u_1_checker_1 (._32_bit_input({{23{1'b0}}, exponent}), .check_1_bit(check_exponent_contains_1));
  _1_checker u_1_checker_2 (._32_bit_input(shifter_1_out), .check_1_bit(check_fraction_contains_1));
  // ALU_12_bit alu_12_bit_1: pin names not known; wires that end beside it: {12{1'b1}}, {3'b111, exponent}, 2'b11, check_exponent_all_1
  Multiplexer #(.width(32)) multiplexer_1 (
    .in0({32{1'b0}}), .in1(fraction), .out(fraction_2), .sel(check_exponent_contains_1));  // open: en
endmodule

module _1_checker (
  input  [31:0] _32_bit_input,
  output check_1_bit
);

  wire n7432_1_p3, n7432_1_p6, n7432_1_p10, n7432_1_p11, n7432_2_p3, n7432_2_p6, n7432_2_p10, n7432_2_p11,
       n7432_3_p3, n7432_3_p6, n7432_3_p10, n7432_3_p11, n7432_4_p3, n7432_4_p6, n7432_4_p10, n7432_4_p11,
       n7432_5_p1, n7432_5_p3, n7432_5_p6, n7432_6_p3, n7432_6_p6, n7432_6_p10, n7432_6_p11, n7432_7_p3,
       n7432_7_p6, n7432_7_p10, n7432_7_p11, n7432_8_p3, n7432_8_p6, n7432_8_p10;

  // _7432 7432_1: pin names not known; wires that end beside it: _32_bit_input[0], _32_bit_input[1], n7432_1_p3, n7432_1_p3, _32_bit_input[2], n7432_1_p6, 1'b0, 1'b1, _32_bit_input[4], n7432_1_p10, n7432_1_p11, _32_bit_input[3], n7432_1_p6, n7432_1_p10
  // _7432 7432_2: pin names not known; wires that end beside it: n7432_1_p11, _32_bit_input[5], n7432_2_p3, n7432_2_p3, _32_bit_input[6], n7432_2_p6, 1'b0, 1'b1, _32_bit_input[8], n7432_2_p10, n7432_2_p11, _32_bit_input[7], n7432_2_p6, n7432_2_p10
  // _7432 7432_3: pin names not known; wires that end beside it: n7432_2_p11, _32_bit_input[9], n7432_3_p3, n7432_3_p3, _32_bit_input[10], n7432_3_p6, 1'b0, 1'b1, _32_bit_input[12], n7432_3_p10, n7432_3_p11, _32_bit_input[11], n7432_3_p6, n7432_3_p10
  // _7432 7432_4: pin names not known; wires that end beside it: n7432_3_p11, _32_bit_input[13], n7432_4_p3, n7432_4_p3, _32_bit_input[14], n7432_4_p6, 1'b0, 1'b1, _32_bit_input[16], n7432_4_p10, n7432_4_p11, _32_bit_input[15], n7432_4_p6, n7432_4_p10
  // _7432 7432_5: pin names not known; wires that end beside it: n7432_5_p1, _32_bit_input[29], n7432_5_p3, n7432_5_p3, _32_bit_input[30], n7432_5_p6, 1'b0, 1'b1, _32_bit_input[31], n7432_5_p6, check_1_bit
  // _7432 7432_6: pin names not known; wires that end beside it: n7432_4_p11, _32_bit_input[17], n7432_6_p3, n7432_6_p3, _32_bit_input[18], n7432_6_p6, 1'b0, 1'b1, _32_bit_input[20], n7432_6_p10, n7432_6_p11, _32_bit_input[19], n7432_6_p6, n7432_6_p10
  // _7432 7432_7: pin names not known; wires that end beside it: n7432_6_p11, _32_bit_input[21], n7432_7_p3, n7432_7_p3, _32_bit_input[22], n7432_7_p6, 1'b0, 1'b1, _32_bit_input[24], n7432_7_p10, n7432_7_p11, _32_bit_input[23], n7432_7_p6, n7432_7_p10
  // _7432 7432_8: pin names not known; wires that end beside it: n7432_7_p11, _32_bit_input[25], n7432_8_p3, n7432_8_p3, _32_bit_input[26], n7432_8_p6, 1'b0, 1'b1, _32_bit_input[28], n7432_8_p10, n7432_5_p1, _32_bit_input[27], n7432_8_p6, n7432_8_p10
endmodule
