// Logisim project ALUSecond (1).circ as structural Verilog: 1 circuit, main circuit main
module main (
  input  Cs0,
  input  Cs1,
  input  Cs2,
  input  A1,
  input  A2,
  input  A3,
  input  A4,
  input  B1,
  input  B2,
  input  B3,
  input  B4,
  output Z,
  output V,
  output C,
  output S1,
  output S2,
  output S3,
  output S4,
  output S
);

  wire main_1_p8, main_1_p9, main_1_p10, main_1_p11, main_1_p12, main_1_p13, main_1_p14, n7432_1_p4,
       n7432_1_p7, n7432_1_p12, n7432_1_p15, n7432_2_p6, n7432_2_p11, n7483_1_p5, n7483_1_p9, n7486_1_p2,
       n7486_1_p3, n7486_1_p6, n7486_1_p11, n7486_1_p14, n7486_2_p4, n7486_2_p9, n7486_2_p12, n74157_1_p4,
       n74157_1_p7, n74157_1_p13, n74157_1_p16, n74157_2_p1, n74157_2_p4, n74157_2_p7, n74157_2_p10,
       n74157_2_p13, n74157_2_p16;

  // ALU_first__main main_1: pin names not known; wires that end beside it: Cs2, Cs1, Cs0, B1, B2, B3, B4, main_1_p8, main_1_p9, main_1_p10, main_1_p11, main_1_p12, main_1_p13, main_1_p14
  // _7486 7486_1: pin names not known; wires that end beside it: A1, n7486_1_p2, n7486_1_p3, A2, n7486_1_p2, n7486_1_p6, 1'b0, 1'b1, n7486_1_p2, A3, n7486_1_p11, n7486_1_p2, A4, n7486_1_p14
  // _7432 7432_1: pin names not known; wires that end beside it: n7486_1_p2, A1, B1, n7432_1_p4, A2, B2, n7432_1_p7, 1'b0, 1'b1, B4, A4, n7432_1_p12, B3, A3, n7432_1_p15
  // _74157 74157_1: pin names not known; wires that end beside it: main_1_p9, n7486_1_p3, n7432_1_p4, n74157_1_p4, n7486_1_p6, n7432_1_p7, n74157_1_p7, 1'b0, 1'b1, 1'b0, n7486_1_p14, n7432_1_p12, n74157_1_p13, n7486_1_p11, n7432_1_p15, n74157_1_p16
  // _74157 74157_2: pin names not known; wires that end beside it: n74157_2_p1, main_1_p11, B1, n74157_2_p4, main_1_p12, B2, n74157_2_p7, 1'b0, 1'b1, n74157_2_p10, main_1_p14, B4, n74157_2_p13, main_1_p13, B3, n74157_2_p16
  // _7483 7483_1: pin names not known; wires that end beside it: 1'b0, 1'b0, 1'b0, 1'b1, n7483_1_p5, 1'b0, 1'b0, 1'b0, n7483_1_p9, 1'b0, n74157_2_p13, n74157_1_p13, S
  // _7483 7483_2: pin names not known; wires that end beside it: 1'b0, S3, n74157_1_p16, n74157_2_p16, 1'b1, S2, n74157_2_p7, n74157_1_p7, 1'b0, n7483_1_p9, main_1_p8, n74157_2_p4, n74157_1_p4, S1
  // _7486 7486_2: pin names not known; wires that end beside it: Cs0, 1'b1, n74157_2_p1, n7486_2_p4, 1'b1, Z, n7483_1_p5, n7483_1_p9, n7486_2_p9, 1'b1, main_1_p9, n7486_2_p12
  // _7432 7432_2: pin names not known; wires that end beside it: main_1_p10, Cs1, n74157_2_p10, S1, S2, n7432_2_p6, 1'b0, 1'b1, S, S3, n7432_2_p11, n7432_2_p11, n7432_2_p6, n7486_2_p4
  // _7408 7408_1: pin names not known; wires that end beside it: main_1_p10, Cs1, n7486_1_p2, 1'b0, 1'b1, n7486_2_p9, n7486_2_p12, V, n7483_1_p5, n7486_2_p12, C, n7483_1_p5

  assign S4 = S;

  // Notes on the sheet:
  //   S1
  //   f
  //   S2
  //   X1
  //   en2
  //   Cin
  //   X2
  //   X3
  //   X4
  //   Y1
  //   Y2
  //   Y3
  //   Y4
  //   Cout
endmodule
