// Logisim project ALUfirst (1).circ as structural Verilog: 1 circuit, main circuit main
module main (
  input  CS2,
  input  CS1,
  input  CS0,
  input  B1,
  input  B2,
  input  B3,
  input  B4,
  output out_8,
  output out_9,
  output out_10,
  output B1_prime,
  output B2_prime,
  output B3_prime,
  output B4_prime
);

  wire n7404_1_p2, n7404_1_p3, n7404_1_p4;

  // _7404 7404_1: pin names not known; wires that end beside it: CS2, n7404_1_p2, n7404_1_p3, n7404_1_p4, B1, B1_prime, 1'b0, 1'b1, B4, B4_prime, B3, B3_prime, B2, B2_prime
  // _7408 7408_1: pin names not known; wires that end beside it: n7404_1_p2, CS1, n7404_1_p3, n7404_1_p4, CS0, out_8, 1'b0, 1'b1, CS0, n7404_1_p3, out_9, CS0, CS2, out_10

  // Notes on the sheet:
  //   Cin
  //   Cs0Cs2
  //   S1
endmodule
